// Logisim project BCD_ADDER.circ as structural Verilog: 3 circuits, main circuit main
module main (
);

  FOUR_BIT_ADDER four_bit_adder_1 ();  // open: CIN, B3, A3, B0, A0, A2, B2, B1, A1, COUT, S2, S1, S3, S0
endmodule

module full_adder (
  input  C,
  input  B,
  input  A,
  output SUM,
  output CARRY
);

  wire and_1_out, and_2_out, and_3_out;

  ExactlyOne xor_1 (.out(SUM), .in0(C), .in1(B), .in2(A));
  and and_1 (and_1_out, A, B);
  and and_2 (and_2_out, B, C);
  and and_3 (and_3_out, C, A);
  ExactlyOne xor_2 (.out(CARRY), .in0(and_1_out), .in1(and_2_out), .in2(and_3_out));
endmodule

module FOUR_BIT_ADDER (
  input  CIN,
  input  B3,
  input  A3,
  input  B0,
  input  A0,
  input  A2,
  input  B2,
  input  B1,
  input  A1,
  output COUT,
  output S2,
  output S1,
  output S3,
  output S0
);

  wire full_adder_2_carry, full_adder_3_carry, full_adder_4_carry;

  full_adder full_adder_1 (.C(full_adder_2_carry), .B(B3), .A(A3), .SUM(S3), .CARRY(COUT));
  full_adder full_adder_2 (.C(full_adder_3_carry), .B(B2), .A(A2), .SUM(S2), .CARRY(full_adder_2_carry));
  full_adder full_adder_3 (.C(full_adder_4_carry), .B(B1), .A(A1), .SUM(S1), .CARRY(full_adder_3_carry));
  full_adder full_adder_4 (.C(CIN), .B(B0), .A(A0), .SUM(S0), .CARRY(full_adder_4_carry));
endmodule
